# Fritzing sketch 02_countSwitching (saved by Fritzing 0.9.3b)
breadboards: 1

parts:
  Switch = Pushbutton [package="[THT]"]
  R1 = Resistor [tolerance=±5% resistance=10k package=THT]
  Arduino = Arduino Uno (Rev3)

nets:
  N1: Switch.Pin_1, Switch.Pin_2, R1.Pin_0, Arduino.D7
  N2: Switch.Pin_3, Switch.Pin_4, Arduino.5V
  N3: R1.Pin_1, Arduino.GND
