# Fritzing sketch 04_control3LEDs (saved by Fritzing 0.9.3b)
breadboards: 1

parts:
  Switch = Pushbutton [package="[THT]"]
  R1 = Resistor [tolerance=±5% resistance=10k package=THT]
  Arduino = Arduino Uno (Rev3)
  LED1 = LED - 5mm [color="Blue (430nm)" package="5 mm [THT]"]
  LED2 = LED - 5mm [color="Green (560nm)" package="5 mm [THT]"]
  LED3 = LED - 5mm [color="Red (633nm)" package="5 mm [THT]"]
  R2 = Resistor [tolerance=±5% resistance=220 package=THT]
  R3 = Resistor [tolerance=±5% resistance=220 package=THT]
  R4 = Resistor [tolerance=±5% resistance=220 package=THT]

nets:
  N1: Switch.Pin_1, Switch.Pin_2, R1.Pin_0, Arduino.D7
  N2: Switch.Pin_3, Switch.Pin_4, Arduino.5V
  N3: R1.Pin_1, Arduino.GND, LED1.cathode, LED2.cathode, LED3.cathode
  N4: Arduino.D8, R4.Pin_1
  N5: Arduino.D9_PWM, R3.Pin_1
  N6: Arduino.D10_PWM/SS, R2.Pin_1
  N7: LED1.anode, R2.Pin_0
  N8: LED2.anode, R3.Pin_0
  N9: LED3.anode, R4.Pin_0
